# Fritzing sketch v1 (saved by Fritzing 0.9.3b)
breadboards: 1

parts:
  VCC2 = 4 x AAA Battery Mount
  S1 = Toggle Switch [package=THT]
  L298N1 = L298N DC motor driver
  M1 = DC Mini Metal Gear Motor
  M2 = DC Mini Metal Gear Motor
  S2 = Pololu QTR-8 Reflectabce Sensor array [package=THT]
  Composant2 = Arduino Mega ADK (Rev3)
  M3 = fc-51 [package=THT]
  M4 = fc-51 [package=THT]

nets:
  N1: VCC2.+, L298N1.12V
  GND: S1.L2, L298N1.GND, S2.pin15, Composant2.GND, M3.pin2, M4.pin2
  N2: L298N1.OUT1, M2.IN2
  N3: L298N1.OUT2, M2.IN1
  N4: L298N1.OUT3, M1.IN2
  N5: L298N1.OUT4, M1.IN1
  5V: L298N1.5V, S2.pin2, S2.pin12, S2.pin13, S2.pin14, S2.pin22, S2.pin23, Composant2.A0, Composant2.VIN, M3.pin3, M4.pin3
  N6: L298N1.ENA, Composant2.D7_PWM
  N7: L298N1.ENB, Composant2.D2_PWM
  N8: L298N1.IN1, Composant2.D6_PWM
  N9: L298N1.IN2, Composant2.D5_PWM
  N10: L298N1.IN3, Composant2.D4_PWM
  N11: L298N1.IN4, Composant2.D3_PWM
  N12: S2.pin5, Composant2.A7
  N13: S2.pin6, Composant2.A6
  N14: S2.pin7, Composant2.A5
  N15: S2.pin8, Composant2.A4
  N16: S2.pin9, Composant2.A3
  N17: S2.pin10, Composant2.A2
  N18: S2.pin11, Composant2.A1
  N19: Composant2.D17/RX2, M4.pin1
  N20: Composant2.D16/TX2, M3.pin1

custom parts:
  L298N DC motor driver: 2x DC motor driver with 78M05 positive voltage regulator (7..35 V) L298N: max 46 V, 2 A Set 5 V Enable jumper to enable 5 V regultor (needed for the L298N) and +5 V output at screw terminal or supply external +5 V at screw terminal Set ENA and/or ENB to +5 V to enable motor permanently or supply ENA and/or ENB with PWM signal IN1 and IN2 set rotation directory for motor A (OUT1/OUT2) IN2 and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
